# Fritzing sketch schematic (saved by Fritzing 0.8.7b)
breadboards: 1

parts:
  Arduino = Arduino Uno (Rev3)
  MIDI_OUT = DIN-5 jack (MIDI) [package=THT]
  SR = 74HC595 [package="DIP16 [THT]"]
  R1 = Resistor [tolerance=±5% resistance=220 package=THT]
  R2 = Resistor [tolerance=±5% resistance=10k package=THT]
  R3 = Resistor [tolerance=±5% resistance=10k package=THT]
  R4 = Resistor [tolerance=±5% resistance=10k package=THT]
  R5 = Resistor [tolerance=±5% resistance=10k package=THT]
  R6 = Resistor [tolerance=±5% resistance=10k package=THT]
  R7 = Resistor [tolerance=±5% resistance=10k package=THT]
  R8 = Resistor [tolerance=±5% resistance=10k package=THT]
  R9 = Resistor [tolerance=±5% resistance=10k package=THT]
  R10 = Resistor [tolerance=±5% resistance=10k package=THT]

nets:
  To Sleeve of Sustain Pedal TRS: Arduino.A0, R10.Pin_0
  Scan Matrix Row 7: Arduino.D8, R8.Pin_0
  Scan Matrix Row 8: Arduino.D9_PWM, R9.Pin_0
  N1: Arduino.D10_PWM/SS, SR.SH_CP
  N2: Arduino.D11_PWM/MOSI, SR.ST_CP
  N3: Arduino.D12/MISO, SR.DS
  GND: Arduino.GND, MIDI_OUT.2, MIDI_OUT.GND, SR.GND, SR.OE, R2.Pin_1, R3.Pin_1, R4.Pin_1, R5.Pin_1, R6.Pin_1, R7.Pin_1, R8.Pin_1, R9.Pin_1, R10.Pin_1
  N4: Arduino.D1/TX, MIDI_OUT.4
  Scan Matrix Row 1: Arduino.D2, R2.Pin_0
  Scan Matrix Row 2: Arduino.D3_PWM, R3.Pin_0
  Scan Matrix Row 3: Arduino.D4, R4.Pin_0
  Scan Matrix Row 4: Arduino.D5_PWM, R5.Pin_0
  Scan Matrix Row 5: Arduino.D6_PWM, R6.Pin_0
  Scan Matrix Row 6: Arduino.D7, R7.Pin_0
  To Tip of Sustain Pedal TRS: Arduino.5V, SR.MR, SR.VCC, R1.Pin_0
  N5: MIDI_OUT.5, R1.Pin_1
  Scan Matrix Column 1: SR.Q1
  Scan Matrix Column 2: SR.Q2
  Scan Matrix Column 3: SR.Q3
  Scan Matrix Column 4: SR.Q4
  Scan Matrix Column 5: SR.Q5
  Scan Matrix Column 6: SR.Q6
  Scan Matrix Column 7: SR.Q7
